// Logisim project main.circ as structural Verilog: 1 circuit, main circuit main
module main (
);

  wire ALUSrcB, ALUSrcB_EX, and_1_out, and_2_out, and_3_out, Auipc, Auipc_EX, Branch_EX, BranchSrc, CLK,
       estagioid_ex_1_p23, estagioid_ex_1_p25, estagioid_ex_1_p26, estagioid_ex_1_p41, estagioid_ex_1_p42,
       estagioid_ex_1_p44, estagioif_id_1_p5, estagioif_id_1_p7, Jalr_EX, Jump_EX, Jump_WB, Lui, Lui_EX,
       MemRead, MemRead_EX, MemToReg, MemToReg_EX, MemWrite, MemWrite_EX, PCSrc_EX, RegWrite_EX, RegWrite_WB,
       Stop, sUnsigned, ucdesvio_1_branchsrc, ucprincipal_1_alusrcb, ucprincipal_1_auipc_uc,
       ucprincipal_1_branch, ucprincipal_1_jump, ucprincipal_1_lui_uc, ucprincipal_1_memread,
       ucprincipal_1_memtoreg, ucprincipal_1_memwrite, ucprincipal_1_pcsrc, ucprincipal_1_regwrite,
       ucprincipal_1_s_jalr, ula_1_szero, undriven;
  wire [1:0] ALUOp, ALUOp_EX, offset, ucenderecamento_1_size, ucprincipal_1_aluop;
  wire [2:0] decodificador_1_funct3, estagioid_ex_1_p43, undriven_2;
  wire [3:0] ucenderecamento_1_byteenable, ucula_1_p5;
  wire [4:0] decodificador_1_rd, decodificador_1_rs1, decodificador_1_rs2, rd_WB;
  wire [6:0] decodificador_1_funct7, decodificador_1_opcode;
  wire [31:0] adder_1_out, adder_2_out, ALU, bancoregistradores_1_ld1, bancoregistradores_1_ld2,
       contadorciclos_1_contador, decodificador_1_imm, estagioid_ex_1_p39, estagioid_ex_1_p40,
       estagioid_ex_1_p45, estagioif_id_1_p8, estagioif_id_1_p9, Imm, LD1, LD2, memdados_1_dados_lidos,
       meminstr_1_instruction, multiplexer_1_out, multiplexer_2_out, multiplexer_3_out, multiplexer_4_out,
       multiplexer_5_out, PC, PC_q, WD;

  Multiplexer #(.width(32)) multiplexer_1 (
    .in0(adder_2_out), .in1(adder_1_out), .out(multiplexer_1_out), .sel(ucprincipal_1_pcsrc));
  Adder #(.width(32)) adder_1 (.a(PC_q), .b(decodificador_1_imm), .out(adder_1_out));  // open: cin, cout
  // Probe on Imm
  and and_1 (and_1_out, CLK, ~Stop);  // AND_Gate
  // Probe on contadorciclos_1_contador
  contadorCiclos contadorciclos_1 (.Clock(and_1_out), .Contador(contadorciclos_1_contador));
  Clock clock_1 (.out(CLK));
  Register #(.width(32)) u_PC (.D(multiplexer_2_out), .en(and_2_out), .clk(and_2_out), .Q(PC_q));  // open: clr
  Multiplexer #(.width(32)) multiplexer_2 (
    .in0(multiplexer_1_out), .in1(ALU), .out(multiplexer_2_out), .sel(ucprincipal_1_s_jalr));
  and and_2 (and_2_out, CLK, ~Stop);  // AND_Gate
  // Probe on PC
  // Probe on LD1
  // Probe on LD2
  // Probe on ALU
  Adder #(.width(32)) adder_2 (.a(32'h4), .b(PC_q), .out(adder_2_out));  // open: cin, cout
  memInstr meminstr_1 (.PC_address(PC_q), .Instruction(meminstr_1_instruction));
  // estagioIF_ID estagioif_id_1: pin names not known; wires that end beside it: adder_2_out, meminstr_1_instruction, PC_q, CLK, estagioif_id_1_p5, estagioif_id_1_p5, estagioif_id_1_p7, estagioif_id_1_p8, estagioif_id_1_p9
  decodificador decodificador_1 (
    .instrucao(estagioif_id_1_p9), .imm(decodificador_1_imm), .opcode(decodificador_1_opcode),
    .rd(decodificador_1_rd), .funct3(decodificador_1_funct3), .rs1(decodificador_1_rs1),
    .rs2(decodificador_1_rs2), .funct7(decodificador_1_funct7));
  ucPrincipal ucprincipal_1 (
    .BranchSrc(undriven), .opcode(decodificador_1_opcode), .MemRead(ucprincipal_1_memread),
    .MemWrite(ucprincipal_1_memwrite), .Jump(ucprincipal_1_jump), .Branch(ucprincipal_1_branch),
    .S_Jalr(ucprincipal_1_s_jalr), .RegWrite(ucprincipal_1_regwrite), .ALUOp(ucprincipal_1_aluop),
    .Auipc_uc(ucprincipal_1_auipc_uc), .ALUSrcB(ucprincipal_1_alusrcb), .Lui_uc(ucprincipal_1_lui_uc),
    .Stop(Stop), .MemToReg(ucprincipal_1_memtoreg), .PCSrc(ucprincipal_1_pcsrc));
  Multiplexer #(.width(32)) multiplexer_3 (.in0(WD), .in1(estagioif_id_1_p8), .out(multiplexer_3_out), .sel(Jump_WB));
  bancoRegistradores bancoregistradores_1 (
    .WD(multiplexer_3_out), .WR(rd_WB), .LD1(bancoregistradores_1_ld1), .LR1(decodificador_1_rs1),
    .LD2(bancoregistradores_1_ld2), .LR2(decodificador_1_rs2), .clk(CLK), .RegWrite(RegWrite_WB));
  // estagioID_EX estagioid_ex_1: pin names not known; wires that end beside it: estagioif_id_1_p7, estagioif_id_1_p8, ucprincipal_1_auipc_uc, ucprincipal_1_lui_uc, ucprincipal_1_pcsrc, ucprincipal_1_jump, ucprincipal_1_aluop, ucprincipal_1_regwrite, ucprincipal_1_alusrcb, ucprincipal_1_memtoreg, ucprincipal_1_memread, ucprincipal_1_memwrite, ucprincipal_1_branch, ucprincipal_1_s_jalr, bancoregistradores_1_ld1, bancoregistradores_1_ld2, decodificador_1_opcode, decodificador_1_rd, decodificador_1_funct3, decodificador_1_funct7, decodificador_1_imm, CLK, estagioid_ex_1_p23, estagioid_ex_1_p23, estagioid_ex_1_p25, estagioid_ex_1_p26, Auipc_EX, Lui_EX, PCSrc_EX, Jump_EX, ALUOp_EX, RegWrite_EX, ALUSrcB_EX, MemToReg_EX, MemRead_EX, MemWrite_EX, Branch_EX, Jalr_EX, estagioid_ex_1_p39, estagioid_ex_1_p40, estagioid_ex_1_p41, estagioid_ex_1_p42, estagioid_ex_1_p43, estagioid_ex_1_p44, estagioid_ex_1_p45, BranchSrc
  // ucULA ucula_1: pin names not known; wires that end beside it: estagioid_ex_1_p41, estagioid_ex_1_p43, estagioid_ex_1_p44, ALUOp, ucula_1_p5
  Multiplexer #(.width(32)) multiplexer_4 (.in0(estagioid_ex_1_p39), .in1(PC), .out(multiplexer_4_out), .sel(Auipc));
  Multiplexer #(.width(32)) multiplexer_5 (
    .in0(multiplexer_4_out), .in1({32{1'b0}}), .out(multiplexer_5_out), .sel(Lui));
  Multiplexer #(.width(32)) multiplexer_6 (
    .in0(estagioid_ex_1_p40), .in1(estagioid_ex_1_p45), .out(LD2), .sel(ALUSrcB));
  ULA ula_1 (.B(LD2), .ALUControl(ucula_1_p5), .A(multiplexer_5_out), .sZero(ula_1_szero), .Result(ALU));
  ucDesvio ucdesvio_1 (.Zero(ula_1_szero), .funct3(undriven_2), .BranchSrc(ucdesvio_1_branchsrc));
  ucEnderecamento ucenderecamento_1 (
    .Adress(ALU), .Funct3(estagioid_ex_1_p43), .writeEnable(MemWrite),
    .byteEnable(ucenderecamento_1_byteenable), .Size(ucenderecamento_1_size), .Offset(offset),
    .signal_unsigned(sUnsigned));
  and and_3 (and_3_out, CLK, ~Stop);  // AND_Gate
  memDados memdados_1 (
    .Endereco(ALU), .clk(and_3_out), .MemRead(MemRead), .byteEnable(ucenderecamento_1_byteenable),
    .dado(estagioid_ex_1_p40), .size(ucenderecamento_1_size), .offset(offset), .sUnsigned(sUnsigned),
    .Dados_lidos(memdados_1_dados_lidos));
  Multiplexer #(.width(32)) multiplexer_7 (.in0(ALU), .in1(memdados_1_dados_lidos), .out(WD), .sel(MemToReg));

  // Notes on the sheet:
  //   PC
  //   rs2
  //   Imm
  //   PC + 4
  //   rd
endmodule
